// Logisim project circuit6_logism.circ as structural Verilog: 1 circuit, main circuit main
module main (
  input  in_1,
  input  in_2,
  input  in_3
);

  wire and_1_out, or_1_out;

  or or_1 (or_1_out, in_1, in_2);
  and and_1 (and_1_out, or_1_out, in_3);
  // NAND_Gate nand_1 has open pins: in2=in_2, in3=and_1_out, out=open
endmodule
